# Fritzing sketch diagram (saved by Fritzing 0.9.6b)
breadboards: 1

parts:
  S1 = Limit Switch [package="Breakout Board"]
  Board = Arduino Pro Micro (Clone)
  Switch = DIP SWITCH [package=dipswitch-02]
  Mode1 = LED - 3mm [color="Red (660nm)" package="3 mm [THT]"]
  Mode3 = LED - 3mm [color="Red (660nm)" package="3 mm [THT]"]
  Mode2 = LED - 3mm [color="Red (660nm)" package="3 mm [THT]"]
  Shift = LED - 3mm [color="Green (560nm)" package="3 mm [THT]"]
  R1 = Resistor [tolerance=±5% resistance=100 package=THT]
  R4 = Resistor [tolerance=±5% resistance=500 package=THT]
  R2 = Resistor [tolerance=±5% resistance=100 package=THT]
  R3 = Resistor [tolerance=±5% resistance=100 package=THT]
  S6 = Limit Switch [package="Breakout Board"]
  S7 = Limit Switch [package="Breakout Board"]
  S8 = Limit Switch [package="Breakout Board"]
  S9 = Limit Switch [package="Breakout Board"]

nets:
  N1: S1.S, Board.D3
  N2: S1.G, Board.GND, Switch.3, Switch.4, Mode1.cathode, Mode3.cathode, Mode2.cathode, Shift.cathode, S6.G, S7.G, S8.G, S9.G
  N3: Board.D2, S6.S
  N4: Board.D4, S7.S
  N5: Board.D5, S9.S
  N6: Board.D6, S8.S
  N7: Board.D8, Switch.2
  N8: Board.D9, Switch.1
  N9: Board.D10, R4.Pin_1
  N10: Board.D16, R3.Pin_1
  N11: Board.D14, R2.Pin_1
  N12: Board.D15, R1.Pin_1
  N13: Mode1.anode, R1.Pin_0
  N14: Mode3.anode, R3.Pin_0
  N15: Mode2.anode, R2.Pin_0
  N16: Shift.anode, R4.Pin_0

custom parts:
  Limit Switch: Generic limit switch commonly found on 3D printers. Typical lever microswitch mounted on a PCB board with a 3 pin JST XH connector.
